// Logisim project oldAutomat.circ as structural Verilog: 1 circuit, main circuit main
module main (
  input  x0,
  input  x1
);

  wire and_1_out, and_2_out, and_3_out, and_4_out, and_5_out, and_6_out, and_7_out, and_8_out, and_9_out,
       and_10_out, and_11_out, and_12_out, and_13_out, and_14_out, and_15_out, and_16_out, and_17_out,
       and_18_out, and_19_out, and_20_out, and_21_out, and_22_out, and_23_out, and_24_out, and_25_out,
       and_26_out, and_27_out, clock_1_out, not_1_out, not_2_out, not_3_out, not_4_out, not_5_out, not_6_out,
       not_7_out, not_8_out, not_9_out, or_1_out, or_2_out, or_3_out, or_4_out, or_5_out, or_6_out, or_7_out,
       q0_q, q1_q, q2_q;

  Clock clock_1 (.out(clock_1_out));
  or or_1 (or_1_out, and_1_out, and_2_out, and_3_out);
  or or_2 (or_2_out, and_4_out, and_5_out, and_6_out);
  or or_3 (or_3_out, and_7_out, and_8_out, and_9_out, and_10_out);
  D_Flip_Flop q2 (.D(or_1_out), .clk(clock_1_out), .Q(q2_q));  // open: Qn, preset, reset
  D_Flip_Flop q1 (.D(or_2_out), .clk(clock_1_out), .Q(q1_q));  // open: Qn, preset, reset
  D_Flip_Flop q0 (.D(or_3_out), .clk(clock_1_out), .Q(q0_q));  // open: Qn, preset, reset
  and and_1 (and_1_out, not_2_out, q2_q);
  and and_2 (and_2_out, q2_q, not_4_out);
  and and_3 (and_3_out, x0, q1_q, q0_q);
  and and_4 (and_4_out, not_2_out, q1_q);
  and and_5 (and_5_out, x0, not_4_out, q0_q);
  and and_6 (and_6_out, not_5_out, q1_q, not_3_out);
  and and_7 (and_7_out, not_2_out, q0_q);
  and and_8 (and_8_out, x0, not_5_out, not_3_out);
  and and_9 (and_9_out, x0, not_4_out, not_3_out);
  and and_10 (and_10_out, not_1_out, not_5_out, not_4_out, q0_q);
  not not_1 (not_1_out, x1);
  not not_2 (not_2_out, x0);
  not not_3 (not_3_out, q0_q);
  not not_4 (not_4_out, q1_q);
  not not_5 (not_5_out, q2_q);
  and and_11 (and_11_out, x0, q2_q, q0_q);
  and and_12 (and_12_out, x0, q1_q, q0_q);
  and and_13 (and_13_out, not_2_out, q2_q, not_3_out);
  and and_14 (and_14_out, not_2_out, q1_q, not_3_out);
  and and_15 (and_15_out, not_2_out, not_5_out, not_4_out, q0_q);
  and and_16 (and_16_out, x0, not_5_out, not_4_out, not_3_out);
  and and_17 (and_17_out, x1, not_5_out, not_4_out, q0_q);
  and and_18 (and_18_out, not_1_out, not_5_out, not_4_out);
  and and_19 (and_19_out, not_2_out, not_5_out, q0_q);
  and and_20 (and_20_out, x0, q1_q, not_3_out);
  and and_21 (and_21_out, not_5_out, not_4_out, not_3_out);
  and and_22 (and_22_out, x0, q2_q, q1_q);
  and and_23 (and_23_out, not_2_out, not_5_out, not_4_out, not_3_out);
  and and_24 (and_24_out, not_2_out, not_4_out);
  and and_25 (and_25_out, q1_q, q0_q);
  and and_26 (and_26_out, x0, not_3_out);
  and and_27 (and_27_out, not_1_out, not_5_out, q0_q);
  or or_4 (or_4_out, and_22_out, and_23_out);
  or or_5 (or_5_out, and_24_out, and_25_out, and_26_out, and_27_out);
  not not_6 (not_6_out, or_6_out);
  or or_6 (or_6_out, and_11_out, and_12_out, and_13_out, and_14_out, and_15_out, and_16_out, and_17_out);
  or or_7 (or_7_out, and_18_out, and_19_out, and_20_out, and_21_out);
  not not_7 (not_7_out, or_7_out);
  not not_8 (not_8_out, or_4_out);
  not not_9 (not_9_out, or_5_out);
  // Probe on not_8_out
  // Probe on not_9_out
  // Probe on not_7_out
  // Probe on not_6_out
  // Probe on not_7_out
  // Probe on not_9_out
  // Probe on not_8_out

  // Notes on the sheet:
  //   Cheat
  //   !x1
  //   x1
  //   !x1
  //   x1
  //   !x1
  //   x1
  //   !x1
  //   x1
  //   !x1
  //   x1
  //   Weiter
  //   !x0
  //   x0
  //   !x0
  //   x0
  //   !x0
  //   x0
  //   x0
  //   !x0
  //   x0
  //   !q0
  //   q0
  //   q0
  //   q0
  //   !x0
  //   q0
  //   !q0
  //   q0
  //   !q0
  //   !q0
  //   !q0
  //   q1
  //   !q1
  //   q1
  //   !q1
  //   q1
  //   !q1
  //   q1
  //   q1
  //   !q1
  //   q2
  //   !q1
  //   !q2
  //   q2
  //   !q2
  //   q2
  //   !q2
  //   q2
  //   !q2
  //   q2
  //   !q2
  //   y3
  //   y2
  //   y1
  //   y0
endmodule
